// Logisim project 4-bitCountdownTimer.circ as structural Verilog: 1 circuit, main circuit main
module main (
  input  E,
  input  CLOCK,
  output Q3,
  output Q2,
  output Q1,
  output Q0
);

  wire button_1_out;

  Button button_1 (.out(button_1_out));
  T_Flip_Flop t_ff_1 (.clk(CLOCK), .T(E), .Q(Q3), .preset(button_1_out));  // open: Qn, reset, en
  T_Flip_Flop t_ff_2 (.clk(Q3), .T(E), .Q(Q2), .preset(button_1_out));  // open: Qn, reset, en
  T_Flip_Flop t_ff_3 (.clk(Q2), .T(E), .Q(Q1), .preset(button_1_out));  // open: Qn, reset, en
  T_Flip_Flop t_ff_4 (.clk(Q1), .T(E), .Q(Q0), .preset(button_1_out));  // open: Qn, reset, en

  // Notes on the sheet:
  //   CLEAR
endmodule
