// Logisim project 4-bitCrescentCounter.circ as structural Verilog: 1 circuit, main circuit main
module main (
  input  E,
  input  CLOCK,
  output Q3,
  output Q2,
  output Q1,
  output Q0
);

  wire button_1_out, t_ff_1_qn, t_ff_2_qn, t_ff_3_qn;

  Button button_1 (.out(button_1_out));
  T_Flip_Flop t_ff_1 (.clk(CLOCK), .T(E), .Q(Q3), .Qn(t_ff_1_qn), .reset(button_1_out));  // open: preset, en
  T_Flip_Flop t_ff_2 (.clk(t_ff_1_qn), .T(E), .Q(Q2), .Qn(t_ff_2_qn), .reset(button_1_out));  // open: preset, en
  T_Flip_Flop t_ff_3 (.clk(t_ff_2_qn), .T(E), .Q(Q1), .Qn(t_ff_3_qn), .reset(button_1_out));  // open: preset, en
  T_Flip_Flop t_ff_4 (.clk(t_ff_3_qn), .T(E), .Q(Q0), .reset(button_1_out));  // open: Qn, preset, en

  // Notes on the sheet:
  //   CLEAR
endmodule
