// Logisim project EncoderDec2BinV1.circ as structural Verilog: 1 circuit, main circuit main
module main (
  output S0,
  output S1,
  output S2,
  output S3
);

  wire _0_out, _1_out, _2_out, _3_out, _4_out, _5_out, _6_out, _7_out, _8_out, _9_out;

  Button _0 (.out(_0_out));
  Button _1 (.out(_1_out));
  Button _2 (.out(_2_out));
  Button _3 (.out(_3_out));
  Button _4 (.out(_4_out));
  Button _5 (.out(_5_out));
  Button _6 (.out(_6_out));
  Button _7 (.out(_7_out));
  Button _8 (.out(_8_out));
  Button _9 (.out(_9_out));
  or or_1 (S0, _1_out, _3_out, _5_out, _7_out, _9_out);
  or or_2 (S1, _2_out, _3_out, _6_out, _7_out);
  or or_3 (S2, _5_out, _4_out, _6_out, _7_out);
  or or_4 (S3, _8_out, _9_out);
  // also tied to GND on the sheet: _0_out
endmodule
