// Logisim project EquivalenceANDgate.circ as structural Verilog: 1 circuit, main circuit main
module main (
  input  A,
  input  B,
  output S1,
  output S2,
  output S3
);

  wire nand_1_out, nor_1_out, nor_2_out;

  and and_1 (S1, A, B);
  nand nand_1 (nand_1_out, A, B);
  nor nor_1 (nor_1_out, A, A);
  nor nor_2 (nor_2_out, B, B);
  nand nand_2 (S2, nand_1_out, nand_1_out);
  nor nor_3 (S3, nor_1_out, nor_2_out);
endmodule
