// Logisim project EquivalenceNOTgate.circ as structural Verilog: 1 circuit, main circuit main
module main (
  input  A,
  output S1,
  output S2,
  output S3
);

  not not_1 (S1, A);
  nand nand_1 (S2, A, A);
  nor nor_1 (S3, A, A);
endmodule
