// Logisim project EquivalenceORgate.circ as structural Verilog: 1 circuit, main circuit main
module main (
  input  A,
  input  B,
  output S1,
  output S2,
  output S3
);

  wire nand_1_out, nand_2_out, nor_1_out;

  or or_1 (S1, A, B);
  nor nor_1 (nor_1_out, A, B);
  nand nand_1 (nand_1_out, A, A);
  nand nand_2 (nand_2_out, B, B);
  nor nor_2 (S2, nor_1_out, nor_1_out);
  nand nand_3 (S3, nand_1_out, nand_2_out);
endmodule
