// Logisim project EquivalenceXNORgate.circ as structural Verilog: 1 circuit, main circuit main
module main (
  input  A,
  input  B,
  output S1,
  output S2,
  output S3
);

  wire nand_1_out, nand_2_out, nand_3_out, nand_4_out, nor_1_out, nor_2_out, nor_3_out, nor_4_out, nor_5_out;

  xnor xnor_1 (S1, A, B);
  nand nand_1 (nand_1_out, A, nand_2_out);
  nand nand_2 (nand_2_out, A, B);
  nand nand_3 (nand_3_out, nand_2_out, B);
  nor nor_1 (nor_1_out, A, A);
  nor nor_2 (nor_2_out, nor_1_out, nor_3_out);
  nor nor_3 (nor_3_out, B, B);
  nor nor_4 (nor_4_out, B, A);
  nand nand_4 (nand_4_out, nand_1_out, nand_3_out);
  nor nor_5 (nor_5_out, nor_2_out, nor_4_out);
  nand nand_5 (S2, nand_4_out, nand_4_out);
  nor nor_6 (S3, nor_5_out, nor_5_out);
endmodule
