// Logisim project FullAdder.circ as structural Verilog: 1 circuit, main circuit main
module main (
  input  C_in,
  input  A,
  input  B,
  input  C_in_2,
  input  A_2,
  input  B_2,
  output S,
  output C_out,
  output S_2,
  output C_out_2
);

  wire and_1_out, and_2_out, and_3_out, and_4_out, and_5_out, xor_1_out, xor_2_out;

  xor xor_1 (xor_1_out, A, B);
  and and_1 (and_1_out, A, B);
  and and_2 (and_2_out, C_in, A);
  and and_3 (and_3_out, C_in, B);
  xor xor_2 (xor_2_out, B_2, A_2);
  xor xor_3 (S, xor_1_out, C_in);
  or or_1 (C_out, and_1_out, and_2_out, and_3_out);
  and and_4 (and_4_out, xor_2_out, C_in_2);
  and and_5 (and_5_out, A_2, B_2);
  xor xor_4 (S_2, xor_2_out, C_in_2);
  or or_2 (C_out_2, and_4_out, and_5_out);
endmodule
