// Logisim project HalfSubtractor.circ as structural Verilog: 1 circuit, main circuit main
module main (
  input  A,
  input  B,
  output S,
  output T_out
);

  wire not_1_out;

  not not_1 (not_1_out, A);
  xor xor_1 (S, A, B);
  and and_1 (T_out, B, not_1_out);
endmodule
