// Logisim project LatchSR.circ as structural Verilog: 1 circuit, main circuit main
module main (
  output Q,
  output Q_prime
);

  wire button_1_out, button_2_out;

  Button button_1 (.out(button_1_out));
  Button button_2 (.out(button_2_out));
  nor nor_1 (Q, button_1_out, Q_prime);
  nor nor_2 (Q_prime, Q, button_2_out);

  // Notes on the sheet:
  //   Reset
  //   Set
endmodule
